// Digital circuit comparador.dig as structural Verilog
module comparador (
  input  [7:0] A,
  input  [7:0] B,
  output C
);

  wire and_1_out, and_2_out, and_3_out, and_4_out, and_5_out, and_6_out, and_7_out, and_8_out;

  and and_1 (and_1_out, A[0], B[0]);
  and and_2 (and_2_out, A[1], B[1]);
  and and_3 (and_3_out, A[2], B[2]);
  and and_4 (and_4_out, A[3], B[3]);
  and and_5 (and_5_out, A[4], B[4]);
  and and_6 (and_6_out, A[5], B[5]);
  and and_7 (and_7_out, A[6], B[6]);
  and and_8 (and_8_out, A[7], B[7]);
  or or_1 (C, and_1_out, and_2_out, and_3_out, and_4_out, and_5_out, and_6_out, and_7_out, and_8_out);
endmodule
