// Digital circuit contador_barra.dig as structural Verilog
module contador_barra (
  input  Start,
  input  Up,
  input  Down,
  output [2:0] Out
);

  wire and_1_out, and_2_out, not_1_out, not_2_out, not_3_out, not_4_out, not_5_out, or_1_out, or_2_out;

  not not_1 (not_1_out, Down);
  not not_2 (not_2_out, Up);
  not not_3 (not_3_out, Start);
  or or_1 (or_1_out, and_1_out, not_1_out);
  or or_2 (or_2_out, and_2_out, not_2_out);
  // _74193 _74193_1: pin names not known; wires that end beside it: 1'b1, or_1_out, or_2_out, 1'b0, 1'b0, 1'b0, 1'b0, not_3_out, 1'b1, 1'b0, Out[0], Out[1], Out[2]
  not not_4 (not_4_out, Out[1]);
  not not_5 (not_5_out, Out[2]);
  and and_1 (and_1_out, not_5_out, not_4_out, Out[0]);
  and and_2 (and_2_out, Out[2], Out[1]);
endmodule
