// Digital circuit contador_reversivel.dig as structural Verilog
module contador_reversivel (
  input  CLOCK,
  input  SET,
  input  RESET,
  input  [2:0] PRESET,
  input  REVERSE,
  output [2:0] OUT,
  output OVERFLOW
);

  wire d_ff_as_1_nq, d_ff_as_1_q, jk_ff_1_q;

  D_FF_AS d_ff_as_1 (.Set(SET), .D(1'b1), .C(1'b1), .Clr(RESET), .Q(d_ff_as_1_q), .nQ(d_ff_as_1_nq));
  JK_FF jk_ff_1 (.J(1'b1), .C(REVERSE), .K(1'b1), .Q(jk_ff_1_q));  // open: nQ
  CounterPreset #(.maxValue(7), .Bits(3)) counterpreset_1 (
    .en(d_ff_as_1_q), .C(~CLOCK), .dir(jk_ff_1_q), .in(PRESET), .ld(SET), .clr(d_ff_as_1_nq), .out(OUT),
    .ovf(OVERFLOW));
endmodule
