// Digital circuit jogo.dig as structural Verilog
module jogo (
  input  clk
);

  wire A_out, D_out, S_out;
  wire [2:0] pong_bloco_1_a;
  wire [7:0] pong_bloco_1_d;

  Button S (.out(S_out));
  Button D (.out(D_out));
  Button A (.out(A_out));
  pong_bloco pong_bloco_1 (.S(S_out), .B1(D_out), .B2(A_out), .CLK(clk), .D(pong_bloco_1_d), .A(pong_bloco_1_a));
  LedMatrix #(.ledPersistence("true")) ledmatrix_1 (.rows(pong_bloco_1_d), .column(pong_bloco_1_a));

  // Notes on the sheet:
  //   clk: Hz: 16
endmodule
