// Digital circuit pong_bloco.dig as structural Verilog
module pong_bloco (
  input  S,
  input  B1,
  input  B2,
  input  CLK,
  output [7:0] D,
  output [2:0] A
);

  wire and_1_out, CLK1, CLK2, comparador_1_c, comparator_1_eq, comparator_2_eq, comparator_3_eq,
       comparator_4_eq, comparator_4_lt, contador_reversivel_1_overflow, contador_reversivel_2_overflow,
       contador_reversivel_3_overflow, d_ff_1_nq, d_ff_1_q, d_ff_2_nq, d_ff_2_q, d_ff_3_nq, d_ff_4_nq, Fail,
       jk_ff_1_q, multiplexer_1_out, priorityencoder_1_num, Reflete;
  wire [2:0] Coluna_W, contador_barra_1_out, contador_reversivel_1_out;
  wire [7:0] Barra, Bola, Bola_R, Linha, multiplexer_2_out, multiplexer_3_out, X_d;

  contador_barra contador_barra_1 (.Start(S), .Up(B1), .Down(B2), .Out(contador_barra_1_out));
  Multiplexer multiplexer_1 (.sel(and_1_out), .in_0(Reflete), .in_1(1'b1), .out(multiplexer_1_out));
  D_FF d_ff_1 (.D(d_ff_1_nq), .C(CLK), .Q(d_ff_1_q), .nQ(d_ff_1_nq));
  contador_reversivel contador_reversivel_1 (
    .CLOCK(CLK1), .SET(S), .RESET(1'b0), .PRESET(3'b100), .REVERSE(contador_reversivel_1_overflow),
    .OUT(contador_reversivel_1_out), .OVERFLOW(contador_reversivel_1_overflow));
  contador_reversivel contador_reversivel_2 (
    .CLOCK(CLK1), .SET(S), .RESET(Fail), .PRESET(3'b000), .REVERSE(multiplexer_1_out), .OUT(Coluna_W),
    .OVERFLOW(contador_reversivel_2_overflow));
  contador_reversivel contador_reversivel_3 (
    .CLOCK(CLK), .SET(S), .RESET(1'b0), .PRESET(3'b000), .REVERSE(contador_reversivel_3_overflow), .OUT(A),
    .OVERFLOW(contador_reversivel_3_overflow));
  D_FF d_ff_2 (.D(d_ff_2_nq), .C(d_ff_1_q), .Q(d_ff_2_q), .nQ(d_ff_2_nq));
  ROM #(.AddrBits(3), .Bits(8)) u_barra (.A(contador_barra_1_out), .sel(1'b1), .D(Barra));
  D_FF d_ff_3 (.D(d_ff_3_nq), .C(d_ff_2_q), .Q(CLK2), .nQ(d_ff_3_nq));
  Decoder #(.Selector_Bits(3)) decoder_1 (
    .sel(contador_reversivel_1_out), .out_0(Linha[0]), .out_1(Linha[1]), .out_2(Linha[2]), .out_3(Linha[3]),
    .out_4(Linha[4]), .out_5(Linha[5]), .out_6(Linha[6]), .out_7(Linha[7]));
  Comparator #(.Bits(3)) comparator_1 (.a(Coluna_W), .b(3'b111), .eq(comparator_1_eq));  // open: gt, lt
  Comparator #(.Bits(3)) comparator_2 (.a(Coluna_W), .b(3'b000), .eq(comparator_2_eq));  // open: gt, lt
  D_FF d_ff_4 (.D(d_ff_4_nq), .C(CLK2), .Q(CLK1), .nQ(d_ff_4_nq));
  D_FF_AS d_ff_as_1 (.Set(comparator_1_eq), .D(1'b1), .C(1'b1), .Clr(S), .Q(Fail));  // open: nQ
  and and_1 (and_1_out, comparator_2_eq, contador_reversivel_2_overflow);
  JK_FF jk_ff_1 (.J(1'b1), .C(CLK2), .K(1'b1), .Q(jk_ff_1_q));  // open: nQ
  Comparator #(.Bits(3)) comparator_3 (.a(Coluna_W), .b(3'b110), .eq(comparator_3_eq));  // open: gt, lt
  comparador comparador_1 (.A(Bola), .B(Barra), .C(comparador_1_c));
  Comparator #(.Bits(3)) comparator_4 (.a(A), .b(3'b111), .eq(comparator_4_eq), .lt(comparator_4_lt));  // open: gt
  Multiplexer #(.Bits(8)) multiplexer_2 (.sel(jk_ff_1_q), .in_0(Linha), .in_1({8{1'b0}}), .out(multiplexer_2_out));
  PriorityEncoder priorityencoder_1 (
    .in0(comparator_4_eq), .in1(comparator_4_lt), .num(priorityencoder_1_num));  // open: any
  ROM #(.AddrBits(3), .Bits(8)) X (.A(A), .sel(1'b1), .D(X_d));
  and and_2 (Reflete, comparator_3_eq, comparador_1_c);
  Multiplexer #(.Bits(8)) multiplexer_3 (
    .sel(priorityencoder_1_num), .in_0(Barra), .in_1(Bola_R), .out(multiplexer_3_out));
  RAMDualAccess #(.AddrBits(3), .Bits(8)) ramdualaccess_1 (
    .str(1'b1), .C(CLK2), .ld(1'b1), .A1(Coluna_W), .Din1(multiplexer_2_out), .A2(A), .D1(Bola), .D2(Bola_R));
  Multiplexer #(.Bits(8)) multiplexer_4 (.sel(Fail), .in_0(multiplexer_3_out), .in_1(X_d), .out(D));

  // Other names for the same wires on the sheet: CLK16 = CLK; Coluna_R[2:0] = A; Dados[7:0] = D; Left = B2;
  //   Right = B1; Start = S

  // Notes on the sheet:
  //   contents of barra (hex, n*v repeats v):
  //   0,e0,70,38,1c,e,7
  //   Para matriz de LEDs
  //   contents of X (hex, n*v repeats v):
  //   0,42,24,18,18,24,42
endmodule
